# Fritzing sketch BME680 PCB (saved by Fritzing 0.9.3b)
circuit board: 3.37211cm x 5.72555cm
breadboards: 1

parts:
  BME680_Header = female pin header, 8 pins [form="♀ (female)"]
  6_Pin_Header = double row female pin header, 6 pins [form="♀ (female)"]

nets:
  N1: BME680_Header.pin3, 6_Pin_Header.pin2
  N2: BME680_Header.pin5, 6_Pin_Header.pin3
  N3: BME680_Header.pin6, 6_Pin_Header.pin4
  N4: BME680_Header.pin8, 6_Pin_Header.pin1

notes:
  Ryan McAdie
  BME680 Hat
