# Fritzing sketch BME680 (saved by Fritzing 0.9.3b)
circuit board: 8.46667cm x 5.64444cm
breadboards: 1

parts:
  BME680 = Adafruit BME680
  Raspberry_Pi_1 = Raspberry Pi 3 [part_number=RPI-3-V1.2]

nets:
  VIN: BME680.VIN, Raspberry_Pi_1.3v3
  GND: BME680.GND, Raspberry_Pi_1.GND
  N1: BME680.SCK/SCL, Raspberry_Pi_1.GPIO3
  N2: BME680.SDI/SDA, Raspberry_Pi_1.GPIO2
