# Fritzing sketch GreenSenseCollabFinal (saved by Fritzing 0.9.3b)
circuit board: 6.56cm x 5.64444cm
breadboards: 1

parts:
  J3 = female pin header, 3 pins [form="♀ (female)"]
  J2 = female pin header, 10 pins [form="♀ (female)"]
  J5 = female pin header, 3 pins [form="♀ (female)"]
  J6 = female pin header, 2 pins [form="♀ (female)"]
  D1 = Zener Diode [part_number=1N4732A breakdown_voltage=3.6V package="300 mil [THT]"]
  Q1 = NPN-Transistor [package="TO92 [THT]"]
  R3 = Resistor [tolerance=±5% resistance=220 package=THT]
  J7 = female pin header, 3 pins [form="♀ (female)"]
  J8 = female pin header, 2 pins [form="♀ (female)"]
  Q2 = NPN-Transistor [package="TO92 [THT]"]
  D2 = Zener Diode [part_number=1N4732A breakdown_voltage=3.6V package="300 mil [THT]"]
  R4 = Resistor [tolerance=±5% resistance=220 package=THT]
  J9 = double row female pin header, 6 pins [form="♀ (female)"]
  U1 = Voltage Regulator - 5V [package="TO220 [THT]"]
  C1 = Capacitor Polarized [package=cpol-radial-10uf-25v]
  C2 = Capacitor Polarized [package=cpol-radial-10uf-25v]
  U2 = Voltage Regulator - 5V [package="TO220 [THT]"]
  C3 = Capacitor Polarized [package=cpol-radial-10uf-25v]
  C4 = Capacitor Polarized [package=cpol-radial-10uf-25v]
  J1 = female pin header, 4 pins [form="♀ (female)"]
  J10 = female pin header, 20 pins [form="♀ (female)"]
  J12 = Power Jack [package=power_jack_pth]
  R6 = Resistor [tolerance=±5% resistance=220 package=THT]

nets:
  N1: J3.pin1, J5.pin1, J10.pin12, R6.Pin_1
  N2: J3.pin2, J10.pin17, R6.Pin_0
  N3: J3.pin3, J5.pin3, J10.pin8
  N4: J2.pin4, J5.pin2
  N5: J2.pin7, J1.pin1, J10.pin19
  N6: J2.pin8, J1.pin2, J10.pin18
  GND: J2.pin9, Q1.E, J7.pin1, Q2.E, U1.GND, C1.-, C2.-, U2.GND, C3.-, C4.-, J1.pin3, J10.pin16, J12.GND, J12.GNDBREAK
  N7: J2.pin10, J1.pin4, J10.pin20
  N8: J6.pin1, D1.anode, Q1.C
  N9: J6.pin2, D1.cathode, J8.pin2, D2.cathode, U1.input_voltage, C1.+, U2.input_voltage, C3.+, J12.PWR
  N10: Q1.B, R3.Pin_0
  N11: R3.Pin_1, J10.pin15
  N12: J7.pin2, U1.output_voltage, C2.+
  N13: J7.pin3, J10.pin6
  N14: J8.pin1, Q2.C, D2.anode
  N15: Q2.B, R4.Pin_0
  N16: R4.Pin_1, J10.pin14
  N17: J9.pin1, J10.pin4
  N18: J9.pin2, J10.pin5
  N19: J9.pin3, U2.output_voltage, C4.+
  N20: J9.pin4, J10.pin1
  N21: J9.pin5, J10.pin2
  N22: J9.pin6, J10.pin3

notes:
  GreenSenseCollabV2
  CENG 355
  Servo
  Stepper
  Temp
  Soil
  BME680
  Fan
  Pump
