# Fritzing sketch GreenSenseSideboard (saved by Fritzing 0.9.3b)
circuit board: 3.1cm x 4.1cm
breadboards: 1

parts:
  PCB_Plug = female pin header, 4 pins [form="♀ (female)"]
  BME680_Header = female pin header, 7 pins [form="♀ (female)"]

nets:
  N1: PCB_Plug.pin1, BME680_Header.pin1
  N2: PCB_Plug.pin2, BME680_Header.pin3
  N3: PCB_Plug.pin3, BME680_Header.pin4
  N4: PCB_Plug.pin4, BME680_Header.pin6

notes:
  GreenSense
  Add-on Board V1
