# Fritzing sketch Raspberry_DS18B20_temperature (saved by Fritzing 0.9.3b)
circuit board: 16.9333cm x 5.64444cm
breadboards: 1

parts:
  R1 = Resistor [tolerance=±5% resistance=4.7k package=THT]
  Raspberry_Pi_1 = Raspberry Pi 3 [part_number=RPI-3-V1.2]
  DS1 = DS18B20 1-Wire Temperature Sensor [part_number=DS18B20]
  R2 = Resistor [tolerance=±5% resistance=220 package=THT]
  LED1 = smd LED [color="Red (633nm)" package="0805 [SMD]"]

nets:
  3V3: R1.Pin_0, Raspberry_Pi_1.3v3, Raspberry_Pi_1.3V3, DS1.VDD
  N1: R1.Pin_1, Raspberry_Pi_1.GPIO4, DS1.DQ
  GND: Raspberry_Pi_1.GND, DS1.GND, LED1.cathode
  N2: Raspberry_Pi_1.GPIO24, R2.Pin_0
  N3: R2.Pin_1, LED1.anode

notes:
  R1 = 4.7kΩ
