# Fritzing sketch SoilMoisturePi (saved by Fritzing 0.9.3b)
circuit board: 3.9cm x 5.6cm
breadboards: 1

parts:
  +Motor- = DC Motor
  Diode = Rectifier Diode [part_number=1N4001 package="300 mil [THT]"]
  R3 = Resistor [tolerance=±5% resistance=1k package=THT]
  Switch = rounded female pin header, 5 pins [form="♀ (female rounded)"]
  ADS1115 = ADS1115
  +Sensor- = Gikfun
  R1 = Resistor [tolerance=±5% resistance=1k package=THT]
  R2 = Resistor [tolerance=±5% resistance=1k package=THT]
  NPN = NPN-Transistor [package="TO92 [THT]"]
  Pi = Raspberry Pi 3 [part_number=RPI-3-V1.2]
  12V_Jack = Power Jack [package=power_jack_pth]

nets:
  N1: +Motor-.pin_1, Diode.cathode, 12V_Jack.PWR
  N2: +Motor-.pin_2, Diode.anode, NPN.C
  N3: R3.Pin_0, Pi.GPIO22
  N4: R3.Pin_1, NPN.B
  3V3: Switch.pin1, ADS1115.VDD, +Sensor-.VCC, R1.Pin_0, Pi.3v3, Pi.3V3
  N5: Switch.pin3, ADS1115.A1
  N6: Switch.pin4, R1.Pin_1, R2.Pin_0
  GND: Switch.pin5, ADS1115.GND, +Sensor-.GND, R2.Pin_1, NPN.E, Pi.GND, 12V_Jack.GND, 12V_Jack.GNDBREAK
  N7: ADS1115.SCL, Pi.GPIO3
  N8: ADS1115.SDA, Pi.GPIO2
  N9: ADS1115.A0, +Sensor-.OUT

notes:
  Daniel Bujold
  Lo
  Med
  Hi
  Vcc and Out labels are mixed on this sensor icon (wire colours are correct)
  6v - 12v supply to barrel jack

custom parts:
  ADS1115: ADC ADS1115
  Gikfun: Gikfun - Capacitive soil moisture sensor
